# Fritzing sketch project (saved by Fritzing 0.9.3b)
breadboards: 2

parts:
  R1 = Resistor [tolerance=±5% resistance=220 package=THT]
  LED1 = LED - 5mm [color="Infrared (940nm)" package="5 mm [THT]"]
  B1 = Infrared LED - 5mm [package="5 mm [THT]"]
  Schrittmotor = 28BYJ-48 Stepper Motor
  RFID_Reader = RFID-RC522-v2
  R3 = Resistor [tolerance=±5% resistance=220 package=THT]
  R4 = Resistor [tolerance=±5% resistance=1k package=THT]
  LED2 = Infrared LED - 5mm [package="5 mm [THT]"]
  B2 = LED - 5mm [color="Infrared (940nm)" package="5 mm [THT]"]
  X1_-_motor_driver = X113647 Stepper Driver Board [package=board]
  R2 = Resistor [tolerance=±5% resistance=1k package=THT]
  M1_-_motor_red = Basic Servo
  M3_-_motor_green = Basic Servo
  M2_-_motor_blue = Basic Servo
  Fließband = Arduino Uno (Rev3) - ICSP [part_number="RFID Modul"]
  Arduino_-_Schließmodul = Arduino Uno (Rev3)
  M5_-_lower_motor = Basic Servo
  M4_-_upper_motor = Basic Servo

nets:
  VCC: R1.Pin_0, X1_-_motor_driver.+V, R2.Pin_0, M1_-_motor_red.vcc, M3_-_motor_green.vcc, M2_-_motor_blue.vcc, Fließband.5V
  N1: R1.Pin_1, LED1.anode
  GND: LED1.cathode, B1.cathode, RFID_Reader.GND, LED2.cathode, B2.cathode, X1_-_motor_driver.GND, M1_-_motor_red.gnd, M3_-_motor_green.gnd, M2_-_motor_blue.gnd, Fließband.GND, Arduino_-_Schließmodul.GND, M5_-_lower_motor.gnd, M4_-_upper_motor.gnd
  N2: B1.anode, R2.Pin_1, Fließband.A5/SCL
  N3: Schrittmotor.RED, X1_-_motor_driver.RED
  N4: Schrittmotor.ORANGE, X1_-_motor_driver.ORANGE
  N5: Schrittmotor.YELLOW, X1_-_motor_driver.YELLOW
  N6: Schrittmotor.PINK, X1_-_motor_driver.PINK
  N7: Schrittmotor.BLUE, X1_-_motor_driver.BLUE
  N8: RFID_Reader.SDA, Fließband.D10_PWM/SS
  N9: RFID_Reader.SCK, Fließband.D13/SCK
  N10: RFID_Reader.MOSI, Fließband.D11_PWM/MOSI
  N11: RFID_Reader.MISO, Fließband.D12/MISO
  N12: RFID_Reader.RST, Fließband.D9_PWM
  3.3V: RFID_Reader.3.3V, Fließband.3V3
  VCC_2: R3.Pin_0, R4.Pin_0, Arduino_-_Schließmodul.5V, M5_-_lower_motor.vcc, M4_-_upper_motor.vcc
  N13: R3.Pin_1, LED2.anode
  N14: R4.Pin_1, B2.anode, Arduino_-_Schließmodul.A0
  N15: X1_-_motor_driver.IN1, Fließband.D2
  N16: X1_-_motor_driver.IN2, Fließband.D3_PWM
  N17: X1_-_motor_driver.IN3, Fließband.D4
  N18: X1_-_motor_driver.IN4, Fließband.D5_PWM
  N19: M1_-_motor_red.pulse, Fließband.D6_PWM
  N20: M3_-_motor_green.pulse, Fließband.D8
  N21: M2_-_motor_blue.pulse, Fließband.D7
  N22: Fließband.D1/TX, Arduino_-_Schließmodul.D1/TX
  N23: Arduino_-_Schließmodul.D2, M4_-_upper_motor.pulse
  N24: Arduino_-_Schließmodul.D3_PWM, M5_-_lower_motor.pulse

notes:
  A1
  A2
  Switch RST / GND
  LED1
  B1
  M1 - red
  M2 - blue
  M3 - green
  M4 - upper
  M5 - lower
  B2
  IR - LED
  IR - Detektor
  A3
  M6
  LS1
  LS2
  X1

custom parts:
  Infrared LED - 5mm: A generic infrared LED (~1.2V)
  RFID-RC522-v2: A simple China made RFID-RC522 Reader; do check the pin labels, as this is a MFRC522 based clone.
  X113647 Stepper Driver Board: A common stepper motor driver board based on ULN2003APG darlington array
