# Fritzing sketch Schaltplan (saved by Fritzing 0.9.3b)
breadboards: 1

parts:
  A1 = Arduino Uno (Rev3) - ICSP
  T1_-_Motortreiber = L9110 H-bridge module [part_number="L9110 H-bridge"]
  A3_-_IR_Modul = FC-03 [chip_label=FC-03]
  A2_-_IR_Modul = FC-03 [chip_label=FC-03]
  M1 = DC Motor
  M2 = DC Motor
  M3 = DC Motor
  M4 = DC Motor

nets:
  N1: A1.A0, A2_-_IR_Modul.D0
  N2: A1.A1, A3_-_IR_Modul.D0
  N3: A1.D2, T1_-_Motortreiber.A-IB
  N4: A1.D3_PWM, T1_-_Motortreiber.A-IA
  N5: A1.D4, T1_-_Motortreiber.B-IA
  N6: A1.D5_PWM, T1_-_Motortreiber.B-IB
  VCC: A1.5V, A1.VIN, T1_-_Motortreiber.VCC, A3_-_IR_Modul.VCC, A2_-_IR_Modul.VCC
  GND: A1.GND, T1_-_Motortreiber.GND, A3_-_IR_Modul.GND, A2_-_IR_Modul.GND
  N7: T1_-_Motortreiber.MOTOR_A-A, M3.pin_1, M4.pin_2
  N8: T1_-_Motortreiber.MOTOR_A-B, M3.pin_2, M4.pin_1
  N9: T1_-_Motortreiber.MOTOR_B-A, M1.pin_1, M2.pin_2
  N10: T1_-_Motortreiber.MOTOR_B-B, M1.pin_2, M2.pin_1

custom parts:
  FC-03: FC-03, LM393 IR Speed Sensor Encoder
