# Fritzing sketch project (saved by Fritzing 0.9.3b)
breadboards: 2

parts:
  R1 = Resistor [tolerance=±5% resistance=220 package=THT]
  IR_-_LED = LED - 5mm [color="Infrared (940nm)" package="5 mm [THT]"]
  IR-Detektor = Infrared LED - 5mm [package="5 mm [THT]"]
  Schrittmotor = 28BYJ-48 Stepper Motor
  RFID_Reader = RFID-RC522-v2
  R3 = Resistor [tolerance=±5% resistance=220 package=THT]
  R4 = Resistor [tolerance=±5% resistance=1k package=THT]
  IR_-_LED_2 = Infrared LED - 5mm [package="5 mm [THT]"]
  IR_-_Detektor = LED - 5mm [color="Infrared (940nm)" package="5 mm [THT]"]
  X1_-_Motortreiber = X113647 Stepper Driver Board [package=board]
  R2 = Resistor [tolerance=±5% resistance=1k package=THT]
  M1_-_Motor_Rot = Basic Servo
  M3_-_Motor_Grün = Basic Servo
  M2_-_Motor_Blau = Basic Servo
  Fließband = Arduino Uno (Rev3) - ICSP [part_number="RFID Modul"]
  Arduino_-_Schließmodul = Arduino Uno (Rev3)
  M5_-_Unterer_Motor = Basic Servo
  M4_-_Oberer_Motor = Basic Servo

nets:
  VCC: R1.Pin_0, X1_-_Motortreiber.+V, R2.Pin_0, M1_-_Motor_Rot.vcc, M3_-_Motor_Grün.vcc, M2_-_Motor_Blau.vcc, Fließband.5V
  N1: R1.Pin_1, IR_-_LED.anode
  GND: IR_-_LED.cathode, IR-Detektor.cathode, RFID_Reader.GND, IR_-_LED_2.cathode, IR_-_Detektor.cathode, X1_-_Motortreiber.GND, M1_-_Motor_Rot.gnd, M3_-_Motor_Grün.gnd, M2_-_Motor_Blau.gnd, Fließband.GND, Arduino_-_Schließmodul.GND, M5_-_Unterer_Motor.gnd, M4_-_Oberer_Motor.gnd
  N2: IR-Detektor.anode, R2.Pin_1, Fließband.A5/SCL
  N3: Schrittmotor.RED, X1_-_Motortreiber.RED
  N4: Schrittmotor.ORANGE, X1_-_Motortreiber.ORANGE
  N5: Schrittmotor.YELLOW, X1_-_Motortreiber.YELLOW
  N6: Schrittmotor.PINK, X1_-_Motortreiber.PINK
  N7: Schrittmotor.BLUE, X1_-_Motortreiber.BLUE
  N8: RFID_Reader.SDA, Fließband.D10_PWM/SS
  N9: RFID_Reader.SCK, Fließband.D13/SCK
  N10: RFID_Reader.MOSI, Fließband.D11_PWM/MOSI
  N11: RFID_Reader.MISO, Fließband.D12/MISO
  N12: RFID_Reader.RST, Fließband.D9_PWM
  3.3V: RFID_Reader.3.3V, Fließband.3V3
  VCC_2: R3.Pin_0, R4.Pin_0, Arduino_-_Schließmodul.5V, M5_-_Unterer_Motor.vcc, M4_-_Oberer_Motor.vcc
  N13: R3.Pin_1, IR_-_LED_2.anode
  N14: R4.Pin_1, IR_-_Detektor.anode, Arduino_-_Schließmodul.A0
  N15: X1_-_Motortreiber.IN1, Fließband.D2
  N16: X1_-_Motortreiber.IN2, Fließband.D3_PWM
  N17: X1_-_Motortreiber.IN3, Fließband.D4
  N18: X1_-_Motortreiber.IN4, Fließband.D5_PWM
  N19: M1_-_Motor_Rot.pulse, Fließband.D6_PWM
  N20: M3_-_Motor_Grün.pulse, Fließband.D8
  N21: M2_-_Motor_Blau.pulse, Fließband.D7
  N22: Fließband.D1/TX, Arduino_-_Schließmodul.D1/TX
  N23: Arduino_-_Schließmodul.D2, M4_-_Oberer_Motor.pulse
  N24: Arduino_-_Schließmodul.D3_PWM, M5_-_Unterer_Motor.pulse

notes:
  Arduino - Abfüllung
  Fließband
  RFID Modul
  Abfüllmodul (3 Servos)
  1x Lichtschranke
  Arduino - Schließmodul
  2 Servos
  RST & GND bitte tauschen
  IR - LED
  IR - Detektor
  M1 - Rot
  M2 - Blau
  M3 - Grün
  M4 - Oben
  M5 - Unten

custom parts:
  Infrared LED - 5mm: A generic infrared LED (~1.2V)
  RFID-RC522-v2: A simple China made RFID-RC522 Reader; do check the pin labels, as this is a MFRC522 based clone.
  X113647 Stepper Driver Board: A common stepper motor driver board based on ULN2003APG darlington array
